// Logisim project Final.circ as structural Verilog: 2 circuits, main circuit main
module main (
  input  [1:0] OutBSel,
  input  [1:0] OutASel,
  input  [1:0] FunSel,
  input  MuxCSel,
  input  [3:0] RegSel,
  input  [3:0] FunSel_2,
  input  [1:0] MuxASEL,
  input  [1:0] MuxBSel,
  input  [1:0] OutCSel,
  output [3:0] OutFlag,
  output [7:0] IR__8_15
);

  wire clk, enable, l_h, read, Z;
  wire [1:0] funsel_AR, funsel_IR, outD_AR;
  wire [2:0] regsel_AR;
  wire [3:0] Adress_Register_File_outc, Adress_Register_File_outc_2, ALU_zcno, multiplexer_1_out,
       multiplexer_1_out_2, multiplexer_2_out, multiplexer_2_out_2, multiplexer_3_out, multiplexer_3_out_2,
       ram_1_data, ram_1_data_2, Register_File_outa, Register_File_outa_2;
  wire [7:0] _16_Bit_Register_out_7, Adress_Register_File_outd, ALU_outalu, Register_File_outb;
  wire [15:0] Instruction;

  Hex_Digit_Display hex_digit_display_1 (.value(multiplexer_2_out_2));  // open: dp
  Hex_Digit_Display hex_digit_display_2 (.value(multiplexer_2_out));  // open: dp
  Hex_Digit_Display hex_digit_display_3 (.value(Register_File_outa));  // open: dp
  Hex_Digit_Display hex_digit_display_4 (.value(Register_File_outa_2));  // open: dp
  Hex_Digit_Display hex_digit_display_5 (.value(_16_Bit_Register_out_7[7:4]));  // open: dp
  _8_bit_register_file_2a__main Register_File (
    .FunSel(FunSel), .Input({multiplexer_2_out_2, multiplexer_2_out}),
    .OutA({Register_File_outa_2, Register_File_outa}), .OutB(Register_File_outb), .OutBSel(OutBSel),
    .OutASel(OutASel), .RegSel(RegSel), .Clock(clk));
  Hex_Digit_Display hex_digit_display_6 (.value(_16_Bit_Register_out_7[3:0]));  // open: dp
  Hex_Digit_Display hex_digit_display_7 (.value(Register_File_outb[7:4]));  // open: dp
  Hex_Digit_Display hex_digit_display_8 (.value(ram_1_data));  // open: dp
  Hex_Digit_Display hex_digit_display_9 (.value(ram_1_data_2));  // open: dp
  Hex_Digit_Display hex_digit_display_10 (.value(Register_File_outb[3:0]));  // open: dp
  Multiplexer #(.width(8), .enable("false")) multiplexer_1 (
    .in0({Adress_Register_File_outc_2, Adress_Register_File_outc}),
    .in1({Register_File_outa_2, Register_File_outa}), .out({multiplexer_1_out_2, multiplexer_1_out}),
    .sel(MuxCSel));
  Multiplexer #(.select(2), .width(8), .enable("false")) multiplexer_2 (
    .in0(_16_Bit_Register_out_7), .in1({ram_1_data_2, ram_1_data}),
    .in2({Adress_Register_File_outc_2, Adress_Register_File_outc}), .in3(ALU_outalu),
    .out({multiplexer_2_out_2, multiplexer_2_out}), .sel(MuxASEL));
  _2_c_main _16_Bit_Register (
    .in_3({ram_1_data_2, ram_1_data}), .out_7({IR__8_15, _16_Bit_Register_out_7}), .low_high(l_h),
    .in_5(funsel_IR[1]), .in_6(funsel_IR[0]), .enable(enable), .clock(clk));
  Hex_Digit_Display hex_digit_display_11 (.value(multiplexer_1_out_2));  // open: dp
  Hex_Digit_Display hex_digit_display_12 (.value(multiplexer_3_out_2));  // open: dp
  Hex_Digit_Display hex_digit_display_13 (.value(multiplexer_3_out));  // open: dp
  Multiplexer #(.select(2), .width(8), .enable("false")) multiplexer_3 (
    .in1(_16_Bit_Register_out_7), .in2({ram_1_data_2, ram_1_data}), .in3(ALU_outalu),
    .out({multiplexer_3_out_2, multiplexer_3_out}), .sel(MuxBSel));  // open: in0
  Hex_Digit_Display hex_digit_display_14 (.value(IR__8_15[7:4]));  // open: dp
  Hex_Digit_Display hex_digit_display_15 (.value(multiplexer_1_out));  // open: dp
  ALU_main ALU (
    .Cin(OutFlag[2]), .A({multiplexer_1_out_2, multiplexer_1_out}), .B(Register_File_outb),
    .FunSel(FunSel_2), .OutAlu(ALU_outalu), .ZCNO(ALU_zcno));
  Hex_Digit_Display hex_digit_display_16 (.value(IR__8_15[3:0]));  // open: dp
  _2b_main Adress_Register_File (
    .FunSel(funsel_AR), .Input({multiplexer_3_out_2, multiplexer_3_out}),
    .OutC({Adress_Register_File_outc_2, Adress_Register_File_outc}), .OutD(Adress_Register_File_outd),
    .OutDSel(outD_AR), .OutCSel(OutCSel), .RegSel(regsel_AR), .Clock(clk));
  Hex_Digit_Display hex_digit_display_17 (.value(Adress_Register_File_outc_2));  // open: dp
  Hex_Digit_Display hex_digit_display_18 (.value(Adress_Register_File_outd[3:0]));  // open: dp
  Hex_Digit_Display hex_digit_display_19 (.value(Adress_Register_File_outd[7:4]));  // open: dp
  Register #(.width(1)) register_1 (.D(ALU_zcno[0]), .en(1'b1), .Q(OutFlag[0]), .clk(clk), .clr(1'b0));
  Register #(.width(1)) register_2 (.D(ALU_zcno[1]), .en(1'b1), .Q(OutFlag[1]), .clk(clk), .clr(1'b0));
  Register #(.width(1)) register_3 (.D(ALU_zcno[2]), .en(1'b1), .Q(OutFlag[2]), .clk(clk), .clr(1'b0));
  Register #(.width(1)) register_4 (.D(ALU_zcno[3]), .en(1'b1), .Q(OutFlag[3]), .clk(clk), .clr(1'b0));
  Hex_Digit_Display hex_digit_display_20 (.value(Adress_Register_File_outc));  // open: dp
  Clock CLOCK (.out(clk));
  Hex_Digit_Display hex_digit_display_21 (.value(ram_1_data_2));  // open: dp
  RAM #(.bus("separate")) ram_1 (
    .addr(Adress_Register_File_outd), .din(ALU_outalu), .data({ram_1_data_2, ram_1_data}), .str(1'b0),
    .clk(clk), .ld(read));  // open: sel, clr
  Hex_Digit_Display hex_digit_display_22 (.value(ram_1_data));  // open: dp
  Control_Unit control_unit_1 (
    .clock(clk), .Z_Flag(Z), .instruction(Instruction), .enable(enable), .l_h(l_h), .\funsel_ır (funsel_IR),
    .regsel_ar(regsel_AR), .funsel_ar(funsel_AR), .outd_ar(outD_AR), .read(read));  // open: out_4

  // Notes on the sheet:
  //   Register File
  //   Input
  //   OutA
  //   IR (0-7)
  //   16-bit Regiter
  //   Input
  //   OutB
  //   AR
  //   Input
  //   A
  //   IR(8-15)
  //   OutD
  //   OutC
  //   Memory Output
endmodule

module Control_Unit (
  input  clock,
  input  Z_Flag,
  input  [15:0] instruction,
  output [2:0] out_4,
  output enable,
  output l_h,
  output [1:0] outd_ar,
  output [1:0] \funsel_ır ,
  output read,
  output [2:0] regsel_ar,
  output [1:0] funsel_ar
);

  wire decoder_4_out0, decoder_4_out1, F1_1, F1_2, F1_3, or_4_out, or_5_out, S1_AR, S1_PC, S1_R0, S1_R1,
       S1_R2, S1_R3, S1_SP, S2_AR, S2_PC, S2_R0, S2_R1, S2_R2, S2_R3, S2_SP, undriven_4, undriven_5,
       undriven_6, undriven_11;
  wire [1:0] BR, CD, undriven_2;
  wire [2:0] F1, F2;
  wire [3:0] Destreg_R, Regsel;
  wire [7:0] AD, adder_1_out, main_1_output, main_2_output, multiplexer_1_out, multiplexer_2_out, undriven,
       undriven_3, undriven_7, undriven_8, undriven_9, undriven_10;

  Multiplexer #(.select(2), .width(8)) multiplexer_1 (
    .in0(adder_1_out), .in1(undriven_3), .in2(main_1_output), .in3(undriven), .out(multiplexer_1_out),
    .sel(2'b00), .en(1'b1));
  _8_bit_register_main main_1 (
    .FunSel(undriven_2), .Input(adder_1_out), .Enable(undriven_4), .Output(main_1_output), .Clock(undriven_5));
  Multiplexer #(.select(2), .width(8)) multiplexer_2 (
    .in0(undriven_7), .in1(undriven_8), .in2(undriven_9), .in3(undriven_10), .out(multiplexer_2_out),
    .sel(CD), .en(undriven_6));
  _8_bit_register_main main_2 (
    .FunSel(2'b01), .Input(multiplexer_1_out), .Enable(1'b1), .Output(main_2_output), .Clock(clock));
  or or_1 (read, F1_1, F1_2);
  Adder adder_1 (.a(main_2_output), .b(8'h1), .out(adder_1_out));  // open: cin, cout
  ROM #(.dataWidth(18)) rom_1 (.addr(main_2_output), .data({F1, F2, CD, BR, AD}), .sel(undriven_11));
  Decoder #(.select(3), .enable("false")) decoder_1 (
    .out1(F1_1), .out2(F1_2), .out3(F1_3), .sel(F1));  // open: out0, out4, out5, out6, out7
  assign funsel_ar = F1_3 ? 2'b10 : 2'bz;  // Controlled_Buffer controlled_buffer_1
  Decoder #(.select(2), .enable("false")) decoder_2 (
    .out0(Regsel[0]), .out1(Regsel[1]), .out2(Regsel[2]), .out3(Regsel[3]), .sel(instruction[10:9]));
  Decoder #(.select(2), .enable("false")) decoder_3 (
    .out0(Destreg_R[0]), .out1(Destreg_R[1]), .out2(Destreg_R[2]), .out3(Destreg_R[3]), .sel(instruction[9:8]));
  Decoder #(.select(2), .enable("false")) decoder_4 (
    .out0(decoder_4_out0), .out1(decoder_4_out1), .out2(out_4[1]), .out3(out_4[2]), .sel(instruction[9:8]));
  or or_2 (out_4[0], decoder_4_out0, decoder_4_out1);
  Decoder #(.select(3), .enable("false")) decoder_5 (
    .out0(S1_R0), .out1(S1_R1), .out2(S1_R2), .out3(S1_R3), .out4(S1_PC), .out5(S1_PC), .out6(S1_AR),
    .out7(S1_SP), .sel(instruction[7:5]));
  assign regsel_ar = F1_3 ? 3'b001 : 3'bz;  // Controlled_Buffer controlled_buffer_2
  or or_3 (enable, F1_1, F1_2);
  Decoder #(.select(3), .enable("false")) decoder_6 (
    .out0(S2_R0), .out1(S2_R1), .out2(S2_R2), .out3(S2_R3), .out4(S2_PC), .out5(S2_PC), .out6(S2_AR),
    .out7(S2_SP), .sel(instruction[4:2]));
  or or_4 (or_4_out, F1_1, F1_2);
  assign \funsel_ır  = or_4_out ? 2'b11 : 2'bz;  // Controlled_Buffer controlled_buffer_3
  assign l_h = F1_1 ? 1'b1 : 1'bz;  // Controlled_Buffer controlled_buffer_4
  assign l_h = F1_2 ? 1'b0 : 1'bz;  // Controlled_Buffer controlled_buffer_5
  or or_5 (or_5_out, F1_1, F1_2);
  assign outd_ar = or_5_out ? 2'b00 : 2'bz;  // Controlled_Buffer controlled_buffer_6

  // Other names for the same wires on the sheet: Adress[7:0] = instruction[7:0]; In0 = instruction[0];
  //   In1 = instruction[1]; In2 = instruction[2]; In3 = instruction[3]; In4 = instruction[4]; In5 = instruction[5];
  //   In6 = instruction[6]; In7 = instruction[7]; clk = clock; Destreg_AR[2:0] = out_4; funsel_IR[1:0] = \funsel_ır ;
  //   AdressMode = instruction[8]; In8 = instruction[8]; In9 = instruction[9]; In10 = instruction[10];
  //   In11 = instruction[11]; In12 = instruction[12]; In13 = instruction[13]; In14 = instruction[14];
  //   In15 = instruction[15]; Z = Z_Flag

  // Notes on the sheet:
  //   MAP
  //    INPUT LOGIC
  //   1
  //   SBR
  //   Funsel
  //   Input
  //   Enable
  //   I
  //   Incrementer
  //   CAR
  //   Z
  //   S
  //   Memory - read
  //   Enable
  //   contents of rom_1 (hex, n*v repeats v):
  //   8001 18002 10003 125*0 8081 18082 10083
  //   AD
  //   BR
  //   CD
  //   Microop
  //   Funsel- AR
  //   Regsel
  //   Destreg
  //   Instruction
  //   Adress mode
  //   0 im 1 dir
  //   Srcreg1
  //   Enable- IR
  //   Regsel- AR
  //   Adress
  //   Srcreg2
  //   Funsel - IR
  //   L/H - IR
  //   OutD- AR
endmodule
